// Logisim project SAP1-Baseline.circ as structural Verilog: 5 circuits, main circuit BuildPlate
module BuildPlate (
  input  in_1,
  input  Run,
  input  WE,
  output [3:0] AddrReg,
  output [7:0] DataIn
);

  wire AccEn, AEn, ALUEn, ALUSe, and_2_out, and_4_out, and_5_out, BEn, CLK, clock_1_out, DisEn, HLT, IE, IO,
       JMP, not_1_out, not_2_out, PCInc, PCO, pull_resistor_1_node, RE, RO;
  wire [3:0] counter_1_q, InstReg_q, register_1_q;
  wire [7:0] H, O, ram_1_dout, T;
  wire [7:4] InstReg_q_2;

  Register #(.width(4)) register_1 (.D(AddrReg), .en(RE), .Q(register_1_q), .clk(CLK));  // open: clr
  RAM #(.addrWidth(4), .trigger("falling"), .\type ("nonvolatile")) ram_1 (
    .addr(register_1_q), .we(WE), .oe(1'b1), .clk(CLK), .din({DataIn[7:4], AddrReg}), .dout(ram_1_dout));
  Pull_Resistor #(.pull(1)) pull_resistor_1 (.node(pull_resistor_1_node));
  Counter #(.max('h4), .width(4)) counter_1 (
    .Q(counter_1_q), .up(pull_resistor_1_node), .clk(not_1_out), .clr(in_1));  // open: load, D, count, carry
  not not_1 (not_1_out, CLK);
  Register InstReg (.D({DataIn[7:4], AddrReg}), .en(IE), .Q({InstReg_q_2, InstReg_q}), .clk(CLK), .clr(in_1));
  ROM #(.dataWidth(12)) MicroCode (
    .addr({InstReg_q_2, counter_1_q}),
    .data({DisEn, IO, IE, RO, RE, BEn, AEn, ALUSe, ALUEn, AccEn, PCInc, PCO}));
  assign AddrReg = IO ? InstReg_q : 4'bz;  // Controlled_Buffer controlled_buffer_1
  // Probe on {DataIn[7:4], AddrReg}
  PCSimplified pcsimplified_1 (
    .CountEn(PCInc), .Clk(CLK), .LoadJump(JMP), .Jump(AddrReg), .PCOut(PCO), .Clear(in_1), .PCBus(AddrReg));
  ALU alu_1 (
    .Clr(in_1), .CLK(CLK), .AEnable(AEn), .A({DataIn[7:4], AddrReg}), .BEnable(BEn), .ALUSelect(ALUSe),
    .B({DataIn[7:4], AddrReg}), .ACCEnable(AccEn), .ALUEnable(ALUEn), .BusLine({DataIn[7:4], AddrReg}));  // open: ZF
  assign {DataIn[7:4], AddrReg} = RO ? ram_1_dout : 8'bz;  // Controlled_Buffer controlled_buffer_2
  and and_1 (HLT, InstReg_q_2[4], InstReg_q_2[5], InstReg_q_2[6], InstReg_q_2[7]);
  Clock clock_1 (.out(clock_1_out));
  and and_2 (and_2_out, Run, clock_1_out);
  Display display_1 (
    .Clk(CLK), .Reset(in_1), .BusLine({DataIn[7:4], AddrReg}), .DisClkEn(DisEn), .Ones(O), .Tens(T),
    .Hundreds(H));
  and and_3 (CLK, and_2_out, not_2_out);
  not not_2 (not_2_out, HLT);
  and and_4 (and_4_out, InstReg_q_2[6], ~InstReg_q_2[7]);  // AND_Gate
  and and_5 (and_5_out, ~counter_1_q[0], counter_1_q[1]);  // AND_Gate
  and and_6 (JMP, and_4_out, and_5_out);
  _7_Segment_Display u_7_segment_display_1 (
    .g(H[6]), .f(H[5]), .a(H[0]), .b(H[1]), .e(H[4]), .d(H[3]), .c(H[2]));  // open: dp
  _7_Segment_Display u_7_segment_display_2 (
    .g(T[6]), .f(T[5]), .a(T[0]), .b(T[1]), .e(T[4]), .d(T[3]), .c(T[2]));  // open: dp
  _7_Segment_Display u_7_segment_display_3 (
    .g(O[6]), .f(O[5]), .a(O[0]), .b(O[1]), .e(O[4]), .d(O[3]), .c(O[2]));  // open: dp

  assign DataIn[3:0] = AddrReg;

  // Other names for the same wires on the sheet: Reset = in_1

  // Notes on the sheet:
  //   34+128+15-73
  //   Example:
  //   2c 0d 0e 1f 30 f0 ...... 22 80 0f 49
  //   contents of MicroCode (hex, n*v repeats v):
  //   81 302 480 140 28 11*0 81 302 480 140 38 11*0 81 302 480 120 12*0 81 302 804 13*0 81 302 402 13*0 81
  //   300 480 102
  //   ADD: 0x
  //   SUB: 1x
  //   DIS: 3
  //   LDA: 2x
  //   JMP: 4x
  //   HLT: F0
endmodule

module MARandRAM (
  input  [3:0] AddrReg,
  input  WE,
  input  AddrRegEn,
  input  OE,
  input  Clk,
  input  [7:0] DataIn,
  output [7:0] BusLine
);

  wire [3:0] register_1_q;
  wire [7:0] ram_1_dout;

  Register #(.width(4)) register_1 (.D(AddrReg), .en(AddrRegEn), .Q(register_1_q), .clk(Clk));  // open: clr
  RAM #(.addrWidth(4), .trigger("falling")) ram_1 (
    .addr(register_1_q), .we(WE), .oe(1'b1), .clk(Clk), .din(DataIn), .dout(ram_1_dout));
  assign BusLine = OE ? ram_1_dout : 8'bz;  // Controlled_Buffer controlled_buffer_1
endmodule

module Display (
  input  [7:0] BusLine,
  input  DisClkEn,
  input  Clk,
  input  Reset,
  output [7:0] Ones,
  output [7:0] Tens,
  output [7:0] Hundreds
);

  wire [7:0] register_1_q;

  Register register_1 (.D(BusLine), .en(DisClkEn), .Q(register_1_q), .clk(Clk), .clr(Reset));
  ROM #(.dataWidth(24)) rom_1 (.addr(register_1_q), .data({Hundreds, Tens, Ones}));

  // Notes on the sheet:
  //   contents of rom_1 (hex, n*v repeats v):
  //   3f3f3f 3f3f06 3f3f5b 3f3f4f 3f3f66 3f3f6d 3f3f7c 3f3f07 3f3f7f 3f3f67 3f063f 3f0606 3f065b 3f064f
  //   3f0666 3f066d 3f067c 3f0607 3f067f 3f0667 3f5b3f 3f5b06 3f5b5b 3f5b4f 3f5b66 3f5b6d 3f5b7c 3f5b07
  //   3f5b7f 3f5b67 3f4f3f 3f4f06 3f4f5b 3f4f4f 3f4f66 3f4f6d 3f4f7c 3f4f07 3f4f7f 3f4f67 3f663f 3f6606
  //   3f665b 3f664f 3f6666 3f666d 3f667c 3f6607 3f667f 3f6667 3f6d3f 3f6d06 3f6d5b 3f6d4f 3f6d66 3f6d6d
  //   3f6d7c 3f6d07 3f6d7f 3f6d67 3f7c3f 3f7c06 3f7c5b 3f7c4f 3f7c66 3f7c6d 3f7c7c 3f7c07 3f7c7f 3f7c67
  //   3f073f 3f0706 3f075b 3f074f 3f0766 3f076d 3f077c 3f0707 3f077f 3f0767 3f7f3f 3f7f06 3f7f5b 3f7f4f
  //   3f7f66 3f7f6d 3f7f7c 3f7f07 3f7f7f 3f7f67 3f673f 3f6706 3f675b 3f674f 3f6766 3f676d 3f677c 3f6707
  //   3f677f 3f6767 63f3f 63f06 63f5b 63f4f 63f66 63f6d 63f7c 63f07 63f7f 63f67 6063f 60606 6065b 6064f
  //   60666 6066d 6067c 60607 6067f 60667 65b3f 65b06 65b5b 65b4f 65b66 65b6d 65b7c 65b07 65b7f 65b67
  //   64f3f 64f06 64f5b 64f4f 64f66 64f6d 64f7c 64f07 64f7f 64f67 6663f 66606 6665b 6664f 66666 6666d
  //   6667c 66607 6667f 66667 66d3f 66d06 66d5b 66d4f 66d66 66d6d 66d7c 66d07 66d7f 66d67 67c3f 67c06
  //   67c5b 67c4f 67c66 67c6d 67c7c 67c07 67c7f 67c67 6073f 60706 6075b 6074f 60766 6076d 6077c 60707
  //   6077f 60767 67f3f 67f06 67f5b 67f4f 67f66 67f6d 67f7c 67f07 67f7f 67f67 6673f 66706 6675b 6674f
  //   66766 6676d 6677c 66707 6677f 66767 5b3f3f 5b3f06 5b3f5b 5b3f4f 5b3f66 5b3f6d 5b3f7c 5b3f07 5b3f7f
  //   5b3f67 5b063f 5b0606 5b065b 5b064f 5b0666 5b066d 5b067c 5b0607 5b067f 5b0667 5b5b3f 5b5b06 5b5b5b
  //   5b5b4f 5b5b66 5b5b6d 5b5b7c 5b5b07 5b5b7f 5b5b67 5b4f3f 5b4f06 5b4f5b 5b4f4f 5b4f66 5b4f6d 5b4f7c
  //   5b4f07 5b4f7f 5b4f67 5b663f 5b6606 5b665b 5b664f 5b6666 5b666d 5b667c 5b6607 5b667f 5b6667 5b6d3f
  //   5b6d06 5b6d5b 5b6d4f 5b6d66 5b6d6d
endmodule

module ALU (
  input  ACCEnable,
  input  ALUEnable,
  input  [7:0] A,
  input  AEnable,
  input  CLK,
  input  [7:0] B,
  input  Clr,
  input  BEnable,
  input  ALUSelect,
  output [7:0] BusLine,
  output ZF
);

  wire [7:0] adder_1_out, multiplexer_1_out, register_1_q, register_2_q, subtractor_1_out;

  Register register_1 (.D(A), .en(AEnable), .Q(register_1_q), .clk(CLK), .clr(Clr));
  assign BusLine = ACCEnable ? register_1_q : 8'bz;  // Controlled_Buffer controlled_buffer_1
  Register register_2 (.D(B), .en(BEnable), .Q(register_2_q), .clk(CLK), .clr(Clr));
  Adder adder_1 (.a(register_1_q), .b(register_2_q), .out(adder_1_out));  // open: cin, cout
  Subtractor subtractor_1 (.a(register_1_q), .b(register_2_q), .out(subtractor_1_out));  // open: bin, bout
  assign BusLine = ALUEnable ? multiplexer_1_out : 8'bz;  // Controlled_Buffer controlled_buffer_2
  Multiplexer #(.width(8)) multiplexer_1 (
    .in0(adder_1_out), .in1(subtractor_1_out), .out(multiplexer_1_out), .sel(ALUSelect));
  nand nand_1 (ZF, multiplexer_1_out[0], multiplexer_1_out[1], multiplexer_1_out[2], multiplexer_1_out[3], multiplexer_1_out[4], multiplexer_1_out[5], multiplexer_1_out[6], multiplexer_1_out[7]);
endmodule

module PCSimplified (
  input  LoadJump,
  input  PCOut,
  input  [3:0] Jump,
  input  Clear,
  input  Clk,
  input  CountEn,
  output [3:0] PCBus
);

  wire and_1_out;
  wire [3:0] counter_1_q;

  and and_1 (and_1_out, Clk, CountEn);
  assign PCBus = PCOut ? counter_1_q : 4'bz;  // Controlled_Buffer controlled_buffer_1
  Counter #(.max('hf), .width(4)) counter_1 (
    .load(LoadJump), .D(Jump), .Q(counter_1_q), .clk(and_1_out), .clr(Clear));  // open: count, carry, up
endmodule
